// Logisim project LC-2200-16.circ as structural Verilog: 5 circuits, main circuit microcontroller
module main (
  input  DrPC,
  input  LdPC,
  input  ALULo,
  input  DrALU,
  input  LdA,
  input  ALUHi,
  input  DrREG,
  input  LdB,
  input  RegSelLo,
  input  DrMEM,
  input  LdMAR,
  input  RegSelHi,
  input  DrOFF,
  input  LdIR,
  input  Clk,
  input  WrMEM,
  input  LdZ,
  input  Clr,
  input  WrREG,
  output [15:0] BUS,
  output [15:0] RegVal,
  output Z,
  output [2:0] OpCode,
  output [3:0] RegNum,
  output [15:0] out_25,
  output [15:0] out_26,
  output [15:0] out_27,
  output [15:0] out_28
);

  wire nor_1_out, not_1_out, not_2_out;
  wire [12:0] IRVal;
  wire [15:0] A_q, B_q, bit_extender_1_out, MAR_q;

  Register #(.width(16), .trigger("falling")) PC (.D(BUS), .en(LdPC), .Q(out_25), .clk(Clk), .clr(Clr));
  assign BUS = DrPC ? out_25 : 16'bz;  // Controlled_Buffer controlled_buffer_1
  Register #(.width(16), .trigger("falling")) A (.D(BUS), .en(LdA), .Q(A_q), .clk(Clk), .clr(Clr));
  _16_bit_ALU u_16_bit_alu_1 (.A(A_q), .B(B_q), .in_3({ALUHi, ALULo}), .out_4(out_26));
  assign BUS = DrALU ? out_26 : 16'bz;  // Controlled_Buffer controlled_buffer_2
  Register #(.width(16), .trigger("falling")) B (.D(BUS), .en(LdB), .Q(B_q), .clk(Clk), .clr(Clr));
  RAM #(.addrWidth(4), .dataWidth(16), .bus("separate")) ram_1 (
    .addr(RegNum), .din(BUS), .data(out_28), .str(WrREG), .clk(Clk), .ld(not_1_out), .clr(Clr));  // open: sel
  not not_1 (not_1_out, WrREG);
  assign BUS = DrREG ? out_28 : 16'bz;  // Controlled_Buffer controlled_buffer_3
  Register #(.width(16), .trigger("falling")) MAR (.D(BUS), .en(LdMAR), .Q(MAR_q), .clk(Clk), .clr(Clr));
  not not_2 (not_2_out, WrMEM);
  RAM #(.addrWidth(16), .dataWidth(16), .bus("separate")) ram_2 (
    .addr(MAR_q), .din(BUS), .data(out_27), .str(WrMEM), .clk(Clk), .ld(not_2_out), .clr(Clr));  // open: sel
  assign BUS = DrMEM ? out_27 : 16'bz;  // Controlled_Buffer controlled_buffer_4
  Register #(.width(16), .trigger("falling")) IR (.D(BUS), .en(LdIR), .Q({OpCode, IRVal}), .clk(Clk), .clr(Clr));
  assign bit_extender_1_out = {{11{IRVal[4]}}, IRVal[4:0]};  // Bit_Extender bit_extender_1
  Register #(.width(1)) u_Z (.D(nor_1_out), .en(LdZ), .Q(Z), .clk(Clk), .clr(Clr));
  nor nor_1 (nor_1_out, BUS[15], BUS[14], BUS[13], BUS[12], BUS[11], BUS[10], BUS[9], BUS[8], BUS[6], BUS[5], BUS[4], BUS[3], BUS[2], BUS[1], BUS[0], BUS[7]);
  assign BUS = DrOFF ? bit_extender_1_out : 16'bz;  // Controlled_Buffer controlled_buffer_5
  Multiplexer #(.select(2), .width(4), .disabled(0), .enable("false")) multiplexer_1 (
    .in0(IRVal[12:9]), .in1(IRVal[8:5]), .in2(IRVal[4:1]), .out(RegNum), .sel({RegSelHi, RegSelLo}));  // open: in3

  assign RegVal = out_28;

  // Other names for the same wires on the sheet: ALUSel[1:0] = {ALUHi, ALULo}; Offset[4:0] = IRVal[4:0];
  //   RZ[3:0] = IRVal[4:1]; IRVal[15:13] = OpCode; RegSel[1:0] = {RegSelHi, RegSelLo}; RX[3:0] = IRVal[12:9];
  //   RY[3:0] = IRVal[8:5]
endmodule

module _1_bit_adder (
  input  in_1,
  input  in_2,
  input  in_3,
  output out_4,
  output out_5
);

  wire and_1_out, and_2_out, xor_1_out;

  and and_1 (and_1_out, in_1, in_2);
  xor xor_1 (xor_1_out, in_1, in_2);
  and and_2 (and_2_out, xor_1_out, in_3);
  xor xor_2 (out_4, xor_1_out, in_3);
  or or_1 (out_5, and_2_out, and_1_out);

  // Other names for the same wires on the sheet: A = in_1; B = in_2; C_IN = in_3; C_OUT = out_5; S = out_4
endmodule

module _16_bit_adder (
  input  [15:0] in_1,
  input  [15:0] in_2,
  input  in_3,
  output [15:0] out_4,
  output out_5
);

  wire n1_bit_adder_2_out_5, n1_bit_adder_3_out_5, n1_bit_adder_4_out_5, n1_bit_adder_5_out_5,
       n1_bit_adder_6_out_5, n1_bit_adder_7_out_5, n1_bit_adder_8_out_5, n1_bit_adder_9_out_5,
       n1_bit_adder_10_out_5, n1_bit_adder_11_out_5, n1_bit_adder_12_out_5, n1_bit_adder_13_out_5,
       n1_bit_adder_14_out_5, n1_bit_adder_15_out_5, n1_bit_adder_16_out_5;

  _1_bit_adder u_1_bit_adder_1 (
    .in_1(n1_bit_adder_2_out_5), .in_2(in_2[15]), .in_3(in_1[15]), .out_4(out_4[15]), .out_5(out_5));
  _1_bit_adder u_1_bit_adder_2 (
    .in_1(n1_bit_adder_4_out_5), .in_2(in_2[14]), .in_3(in_1[14]), .out_4(out_4[14]),
    .out_5(n1_bit_adder_2_out_5));
  _1_bit_adder u_1_bit_adder_3 (
    .in_1(n1_bit_adder_6_out_5), .in_2(in_2[12]), .in_3(in_1[12]), .out_4(out_4[12]),
    .out_5(n1_bit_adder_3_out_5));
  _1_bit_adder u_1_bit_adder_4 (
    .in_1(n1_bit_adder_3_out_5), .in_2(in_2[13]), .in_3(in_1[13]), .out_4(out_4[13]),
    .out_5(n1_bit_adder_4_out_5));
  _1_bit_adder u_1_bit_adder_5 (
    .in_1(n1_bit_adder_7_out_5), .in_2(in_2[10]), .in_3(in_1[10]), .out_4(out_4[10]),
    .out_5(n1_bit_adder_5_out_5));
  _1_bit_adder u_1_bit_adder_6 (
    .in_1(n1_bit_adder_5_out_5), .in_2(in_2[11]), .in_3(in_1[11]), .out_4(out_4[11]),
    .out_5(n1_bit_adder_6_out_5));
  _1_bit_adder u_1_bit_adder_7 (
    .in_1(n1_bit_adder_8_out_5), .in_2(in_2[9]), .in_3(in_1[9]), .out_4(out_4[9]),
    .out_5(n1_bit_adder_7_out_5));
  _1_bit_adder u_1_bit_adder_8 (
    .in_1(n1_bit_adder_9_out_5), .in_2(in_2[8]), .in_3(in_1[8]), .out_4(out_4[8]),
    .out_5(n1_bit_adder_8_out_5));
  _1_bit_adder u_1_bit_adder_9 (
    .in_1(n1_bit_adder_10_out_5), .in_2(in_2[7]), .in_3(in_1[7]), .out_4(out_4[7]),
    .out_5(n1_bit_adder_9_out_5));
  _1_bit_adder u_1_bit_adder_10 (
    .in_1(n1_bit_adder_11_out_5), .in_2(in_2[6]), .in_3(in_1[6]), .out_4(out_4[6]),
    .out_5(n1_bit_adder_10_out_5));
  _1_bit_adder u_1_bit_adder_11 (
    .in_1(n1_bit_adder_12_out_5), .in_2(in_2[5]), .in_3(in_1[5]), .out_4(out_4[5]),
    .out_5(n1_bit_adder_11_out_5));
  _1_bit_adder u_1_bit_adder_12 (
    .in_1(n1_bit_adder_14_out_5), .in_2(in_2[4]), .in_3(in_1[4]), .out_4(out_4[4]),
    .out_5(n1_bit_adder_12_out_5));
  _1_bit_adder u_1_bit_adder_13 (
    .in_1(n1_bit_adder_16_out_5), .in_2(in_2[2]), .in_3(in_1[2]), .out_4(out_4[2]),
    .out_5(n1_bit_adder_13_out_5));
  _1_bit_adder u_1_bit_adder_14 (
    .in_1(n1_bit_adder_13_out_5), .in_2(in_2[3]), .in_3(in_1[3]), .out_4(out_4[3]),
    .out_5(n1_bit_adder_14_out_5));
  _1_bit_adder u_1_bit_adder_15 (
    .in_1(in_3), .in_2(in_2[0]), .in_3(in_1[0]), .out_4(out_4[0]), .out_5(n1_bit_adder_15_out_5));
  _1_bit_adder u_1_bit_adder_16 (
    .in_1(n1_bit_adder_15_out_5), .in_2(in_2[1]), .in_3(in_1[1]), .out_4(out_4[1]),
    .out_5(n1_bit_adder_16_out_5));

  // Other names for the same wires on the sheet: A[15:0] = in_1; B[15:0] = in_2; C_IN = in_3; C_OUT = out_5;
  //   S[15:0] = out_4
endmodule

module _16_bit_ALU (
  input  [15:0] A,
  input  [15:0] B,
  input  [1:0] in_3,
  output [15:0] out_4
);

  wire [15:0] and_1_out, n16_bit_adder_1_out_4, n16_bit_adder_2_out_4, nand_1_out, not_1_out;

  _16_bit_adder u_16_bit_adder_1 (.in_1(A), .in_2(B), .in_3(1'b0), .out_4(n16_bit_adder_1_out_4));  // open: out_5
  assign and_1_out = A & not_1_out;  // AND_Gate and_1, 16 bits wide
  assign not_1_out = ~B;  // NOT_Gate not_1, 16 bits wide
  _16_bit_adder u_16_bit_adder_2 (.in_1(A), .in_2(16'h1), .in_3(1'b0), .out_4(n16_bit_adder_2_out_4));  // open: out_5
  assign nand_1_out = ~(A & B);  // NAND_Gate nand_1, 16 bits wide
  Multiplexer #(.select(2), .width(16), .disabled(0), .enable("false")) multiplexer_1 (
    .in0(n16_bit_adder_1_out_4), .in1(nand_1_out), .in2(and_1_out), .in3(n16_bit_adder_2_out_4), .out(out_4),
    .sel(in_3));

  // Other names for the same wires on the sheet: Out[15:0] = out_4; Sel[1:0] = in_3

  // Notes on the sheet:
  //   Add
  //   Sub
  //   Incr
  //   Nand
endmodule

module microcontroller (
  input  CLR
);

  wire ALUHi, ALULo, clk, DrALU, DrMEM, DrOFF, DrPC, DrREG, LdA, LdB, LdIR, LdMAR, LdPC, LdZ, RegSelHi,
       RegSelLo, WrMEM, WrREG;
  wire [0:0] main_1_z;
  wire [1:0] rom_1_data;
  wire [2:0] main_1_opcode;
  wire [5:0] multiplexer_1_out, register_1_q, rom_1_data_2, rom_2_data, rom_3_data;

  Multiplexer #(.select(2), .width(6), .disabled(0), .enable("false")) multiplexer_1 (
    .in0(rom_1_data_2), .in1(rom_3_data), .in2(rom_2_data), .out(multiplexer_1_out), .sel(rom_1_data));  // open: in3
  Register #(.width(6), .trigger("falling")) register_1 (
    .D(multiplexer_1_out), .Q(register_1_q), .clk(clk));  // open: en, clr
  ROM #(.addrWidth(6), .dataWidth(25)) rom_1 (
    .addr(register_1_q),
    .data({rom_1_data, ALUHi, ALULo, RegSelHi, RegSelLo, WrMEM, WrREG, LdZ, LdB, LdA, LdMAR, LdIR, LdPC, DrOFF, DrPC, DrALU, DrMEM, DrREG, rom_1_data_2}));  // open: sel
  ROM #(.addrWidth(2), .dataWidth(6)) rom_2 (.addr({1'b0, main_1_z[0]}), .data(rom_2_data));  // open: sel
  main main_1 (
    .DrPC(DrPC), .LdPC(LdPC), .ALULo(ALULo), .DrALU(DrALU), .LdA(LdA), .ALUHi(ALUHi), .DrREG(DrREG),
    .LdB(LdB), .RegSelLo(RegSelLo), .DrMEM(DrMEM), .LdMAR(LdMAR), .RegSelHi(RegSelHi), .DrOFF(DrOFF),
    .LdIR(LdIR), .WrMEM(WrMEM), .Z(main_1_z[0]), .LdZ(LdZ), .WrREG(WrREG), .OpCode(main_1_opcode), .Clr(CLR),
    .Clk(clk));  // open: BUS, RegVal, RegNum, out_25, out_27, out_26, out_28
  ROM #(.addrWidth(3), .dataWidth(6)) rom_3 (.addr(main_1_opcode), .data(rom_3_data));  // open: sel
  Clock clock_1 (.out(clk));

  // Notes on the sheet:
  //   contents of rom_1 (hex, n*v repeats v):
  //   6201 1082 e00900 84044 108045 20100 84047 8408 20100 8404a 10804b 220100 8404d 840e 210f 20080 84051
  //   8412 2113 40040 4055 88056 1410100 4218 8419 900 0 a021c 840 1d
  //   contents of rom_2 (hex, n*v repeats v):
  //   1a 17
  //   contents of rom_3 (hex, n*v repeats v):
  //   3 9 6 c 10 14 1b 1d
endmodule
